# Fritzing sketch circuit (saved by Fritzing 0.9.4)
breadboards: 1

parts:
  Bauteil1 = Arduino Nano (Rev3.0) (ICSP)
  TD-er1 = MH-Z19 CO2 sensor [part_number=MH-Z19]
  LED_Matrix_MAX7219 = LED Matrix - Serial Interface - Red/Green/Blue
  R1 = Resistor [tolerance=±5% resistance=100k package="0805 [SMD]"]
  S1 = SWITCH-MOMENTARY-2 [package=tactile-pth-12mm]
  Button_for_digits = SWITCH-MOMENTARY-2 [package=tactile-pth]

nets:
  N1: Bauteil1.D1/TX, TD-er1.RX
  N2: Bauteil1.D0/RX, TD-er1.TX
  GND: Bauteil1.GND, Bauteil1.D4, TD-er1.GND, LED_Matrix_MAX7219.GND
  N3: Bauteil1.D10, LED_Matrix_MAX7219.MOSI
  5V: Bauteil1.5V, TD-er1.Vin, LED_Matrix_MAX7219.VCC
  N4: Bauteil1.3V3, S1.1, Button_for_digits.1
  N5: Bauteil1.D13/SCK, LED_Matrix_MAX7219.CS
  N6: Bauteil1.D11/MOSI, LED_Matrix_MAX7219.MISO
  N7: R1.Pin_0, S1.2, Button_for_digits.2

notes:
  -DIN
  -CS
  -CLK
